# Fritzing sketch 회로 (saved by Fritzing 0.9.3b)
breadboards: 1

parts:
  부품1 = Arduino Mega 2560 (Rev3)
  U2 = LCD-16X2 [package=lcd-16x2_noholes]
  R1 = Trimmer Potentiometer [maximum_resistance=10kΩ package=THT]
  부품2 = Bluetooth HC-05 Macho
  부품3 = RFID USB Reader
  J1 = Piezo Speaker
  LED1 = RGB LED (com. anode, rbg) [package="5 mm [THT]"]

nets:
  N1: 부품1.D19/RX1, 부품2.TXD
  N2: 부품1.D18/TX1, 부품2.RXD
  N3: 부품1.D13_PWM, LED1.red_cathode
  N4: 부품1.D11_PWM, LED1.green_cathode
  N5: 부품1.D10_PWM, J1.pin2
  N6: 부품1.D8_PWM, U2.DB7
  3V3: 부품1.3V3, 부품3.VCC
  5V: 부품1.5V, U2.VDD, U2.A, R1.leg1, 부품2.VCC
  GND: 부품1.GND, U2.VSS, U2.R_W, U2.K, R1.leg2, 부품2.GND, 부품3.TX-O, J1.pin1, LED1.common_anode
  N7: 부품1.D2_PWM, U2.RS
  N8: 부품1.D3_PWM, U2.E
  N9: 부품1.D4_PWM, U2.DB4
  N10: 부품1.D5_PWM, 부품3.GND
  N11: 부품1.D6_PWM, U2.DB5
  N12: 부품1.D7_PWM, U2.DB6
  N13: 부품1.D50, 부품3.ANT1
  N14: 부품1.D51, 부품3.ANT2
  N15: 부품1.D52, 부품3.CP
  N16: 부품1.D53, 부품3.GNDT
  N17: U2.VO, R1.wiper
